// Logisim project 658_Computer.circ as structural Verilog
module Microcontroller (
  input  in_1,
  input  in_2,
  input  in_3,
  input  in_4,
  input  in_5,
  input  in_6,
  input  in_7,
  input  in_8,
  input  in_9,
  input  in_10,
  input  in_11,
  input  in_12,
  input  in_13
);

  wire A_128K, A_128K_B, and_1_out, and_2_out, and_3_out, and_4_out, and_10_out, and_11_out, BANK_LATCH,
       CS0_B, CS1_B, CS2_B, CS3_B, DATA_TRANSMIT_B, DEVICE_ADDRESS_VALID_B, FETCH_OPCODE, FST,
       IDMEM_KERNAL_MODE_B, IDMEM_OUT_INTERRUPTS_B, IDMEM_USER_BANK_B, internal_memory_glue_1_ceb,
       internal_memory_glue_1_oeb, internal_memory_glue_1_web, IRQ_B, KERNAL_MODE, KERNAL_MODE_B,
       microprocessor_w65c816_1_p8, microprocessor_w65c816_1_p11, microprocessor_w65c816_1_p12,
       microprocessor_w65c816_1_p13, MRAM_ACCESS_B, MRAM_VALID_ADDRESS, MRAM_VALID_ADDRESS_B, MREAD, MREADY,
       MVALID, MWRITE, n8_bit_bi_latch_lvc543_1_p8, nand_1_out, nand_3_out, nand_4_out, nand_7_out,
       nand_8_out, NMI_B, nor_1_out, nor_2_out, nor_3_out, not_13_out, not_14_out, not_15_out, not_16_out,
       not_17_out, not_18_out, not_19_out, not_20_out, not_21_out, not_26_out, not_27_out, not_28_out,
       not_29_out, not_30_out, or_1_out, or_2_out, or_3_out, or_4_out, or_5_out, or_8_out, or_9_out, PHI2,
       pull_resistor_1_node, pull_resistor_2_node, pull_resistor_3_node, pull_resistor_4_node,
       pull_resistor_5_node, pull_resistor_13_node, pull_resistor_14_node, pull_resistor_15_node,
       pull_resistor_18_node, pull_resistor_19_node, pull_resistor_20_node, pull_resistor_21_node, RDY,
       READ_BANK_REMAP, READ_ENABLE, READ_ENABLE_B, RESET, RESET_1, RWB, RWB_B, SEL0, SEL1, SEL2, SEL3, SEL4,
       SEL5, SEL6, SEL7, SEL9, VALID_ADDRESS, VPB, WRITE_ENABLE, WRITE_ENABLE_B;
  wire [3:0] not_9_out;
  wire [7:0] A0_7, A8_15, BA0_7, buffer_2_out, D, IRAM_A0_7, MRAM_A16_23, n3_to_8_decoder_lvc138_1_p5,
       n8_bit_bi_latch_lvc543_1_p5, not_1_out, OUT_INTERRUPTS, pull_resistor_6_node, ram_3_data, USER_BANK;
  wire [7:2] n3_to_8_decoder_lvc138_2_p5;
  wire [7:4] n3_to_8_decoder_lvc138_3_p5;
  wire [16:0] internal_memory_glue_1_address_out_a0_16;
  wire [23:0] MRAM_A;

  not not_1 (not_1_out[0], in_2);
  not not_2 (not_1_out[1], in_3);
  not not_3 (not_1_out[2], in_4);
  not not_4 (not_1_out[3], in_5);
  not not_5 (not_1_out[4], in_6);
  not not_6 (not_1_out[5], in_7);
  not not_7 (not_1_out[6], in_8);
  not not_8 (not_1_out[7], in_9);
  not not_9 (not_9_out[0], in_10);
  not not_10 (not_9_out[1], in_11);
  not not_11 (not_9_out[2], in_12);
  not not_12 (not_9_out[3], in_13);
  Timing_Circuit timing_circuit_1 (
    .SELECTOR({SEL9, MRAM_ACCESS_B, SEL7, SEL6, SEL5, SEL4, SEL3, SEL2, SEL1, SEL0}), .RST(RESET),
    .RST_1(RESET_1), .CLK(FST), .RESET(in_1));  // open: CLK_B, HCLK, HCLK_B, MULTIPLEXER, COUNTER, RSTB
  not not_13 (not_13_out, A8_15[3]);
  not not_14 (not_14_out, BA0_7[0]);
  not not_15 (not_15_out, BA0_7[1]);
  not not_16 (not_16_out, BA0_7[2]);
  not not_17 (not_17_out, BA0_7[3]);
  not not_18 (not_18_out, BA0_7[4]);
  not not_19 (not_19_out, BA0_7[5]);
  not not_20 (not_20_out, BA0_7[6]);
  not not_21 (not_21_out, BA0_7[7]);
  Interrupt_Vectoring interrupt_vectoring_1 (
    .IRQ_B(IRQ_B), .NMI_B(NMI_B), .ADDRESS_OUT_A0_7(IRAM_A0_7), .ADDRESS_IN_A0_7(A0_7), .VPB(VPB),
    .IRQ_0_B(not_1_out[0]), .IRQ_1_B(not_1_out[1]), .IRQ_2_B(not_1_out[2]), .IRQ_3_B(not_1_out[3]),
    .IRQ_4_B(not_1_out[4]), .IRQ_5_B(not_1_out[5]), .IRQ_6_B(not_1_out[6]), .IRQ_7_B(not_1_out[7]),
    .NMI_0_B(not_9_out[0]), .NMI_1_B(not_9_out[1]), .NMI_2_B(not_9_out[2]), .NMI_3_B(not_9_out[3]));
  Pull_Resistor #(.pull(1)) pull_resistor_1 (.node(pull_resistor_1_node));
  nand nand_1 (nand_1_out, A0_7[7], A8_15[0], A8_15[1], A8_15[2]);
  Pull_Resistor #(.pull(1)) pull_resistor_2 (.node(pull_resistor_2_node));
  Pull_Resistor #(.pull(1)) pull_resistor_3 (.node(pull_resistor_3_node));
  and and_1 (and_1_out, A8_15[4], A8_15[5], A8_15[6], A8_15[7]);
  and and_2 (and_2_out, not_14_out, not_15_out, not_16_out, not_17_out);
  and and_3 (and_3_out, not_18_out, not_19_out, not_20_out, not_21_out);
  and and_4 (and_4_out, not_17_out, not_16_out, not_15_out, pull_resistor_1_node);
  and and_5 (PHI2, SEL0, SEL1);
  not not_22 (BANK_LATCH, SEL1);
  nand nand_2 (DATA_TRANSMIT_B, SEL0, SEL1, SEL2, SEL3);
  not not_23 (READ_BANK_REMAP, SEL3);
  nand nand_3 (nand_3_out, SEL7, pull_resistor_2_node);
  nand nand_4 (nand_4_out, SEL7, MRAM_ACCESS_B, pull_resistor_3_node);
  // _3_to_8_Decoder__LVC138 3_to_8_decoder_lvc138_1: pin names not known; wires that end beside it: KERNAL_MODE_B, DEVICE_ADDRESS_VALID_B, A0_7[6:4], nand_1_out, n3_to_8_decoder_lvc138_1_p5
  and and_6 (WRITE_ENABLE, VALID_ADDRESS, RWB_B, nand_3_out);
  and and_7 (READ_ENABLE, nand_4_out, RWB, VALID_ADDRESS);
  nand nand_5 (DEVICE_ADDRESS_VALID_B, not_13_out, and_1_out, and_2_out, and_3_out);
  nand nand_6 (A_128K_B, and_4_out, and_3_out);
  and and_8 (A_128K, and_4_out, and_3_out);
  not not_24 (WRITE_ENABLE_B, WRITE_ENABLE);
  not not_25 (READ_ENABLE_B, READ_ENABLE);
  Pull_Resistor #(.pull(1)) pull_resistor_4 (.node(pull_resistor_4_node));
  // _3_to_8_Decoder__LVC138 3_to_8_decoder_lvc138_2: pin names not known; wires that end beside it: n3_to_8_decoder_lvc138_1_p5[0], A0_7[3], A0_7[2:0], pull_resistor_4_node, {n3_to_8_decoder_lvc138_2_p5[7:4], IDMEM_OUT_INTERRUPTS_B, n3_to_8_decoder_lvc138_2_p5[2], IDMEM_USER_BANK_B, IDMEM_KERNAL_MODE_B}, n3_to_8_decoder_lvc138_2_p5[2]
  Pull_Resistor #(.pull(1)) pull_resistor_5 (.node(pull_resistor_5_node));
  // Microprocessor__W65C816 microprocessor_w65c816_1: pin names not known; wires that end beside it: pull_resistor_5_node, IRQ_B, NMI_B, RESET_1, PHI2, 64'h239093209053202, {A8_15, A0_7}, microprocessor_w65c816_1_p8, RWB, RDY, microprocessor_w65c816_1_p11, microprocessor_w65c816_1_p12, microprocessor_w65c816_1_p13, FST, VPB
  Pull_Resistor #(.pull(1)) pull_resistor_6 (.node(pull_resistor_6_node));
  assign pull_resistor_6_node = D;  // Buffer buffer_1, 8 bits wide
  // Probe on {A8_15, A0_7}
  // Probe on microprocessor_w65c816_1_p8
  Pull_Resistor #(.pull(1)) pull_resistor_7 (.node(microprocessor_w65c816_1_p13));
  Pull_Resistor pull_resistor_8 (.node(microprocessor_w65c816_1_p11));
  Pull_Resistor pull_resistor_9 (.node(microprocessor_w65c816_1_p12));
  Pull_Resistor #(.pull(1)) pull_resistor_10 (.node(VPB));
  Pull_Resistor #(.pull(1)) pull_resistor_11 (.node(RWB));
  Pull_Resistor #(.pull(1)) pull_resistor_12 (.node(RDY));
  or or_1 (or_1_out, IDMEM_USER_BANK_B, READ_ENABLE_B);
  Pull_Resistor pull_resistor_13 (.node(pull_resistor_13_node));
  nor nor_1 (nor_1_out, IDMEM_USER_BANK_B, WRITE_ENABLE);
  or or_2 (or_2_out, IDMEM_KERNAL_MODE_B, READ_ENABLE_B);
  not not_26 (not_26_out, RESET);
  not not_27 (not_27_out, VPB);
  not not_28 (not_28_out, WRITE_ENABLE);
  not not_29 (not_29_out, VPB);
  not not_30 (not_30_out, RESET);
  or or_3 (or_3_out, IDMEM_OUT_INTERRUPTS_B, READ_ENABLE_B);
  nor nor_2 (nor_2_out, IDMEM_OUT_INTERRUPTS_B, WRITE_ENABLE);
  Pull_Resistor pull_resistor_14 (.node(pull_resistor_14_node));
  or or_4 (or_4_out, not_26_out, not_27_out, nor_3_out);
  nor nor_3 (nor_3_out, not_28_out, IDMEM_KERNAL_MODE_B);
  or or_5 (or_5_out, pull_resistor_6_node[0], not_29_out, not_30_out);
  Pull_Resistor pull_resistor_15 (.node(pull_resistor_15_node));
  Pull_Resistor pull_resistor_16 (.node({A8_15, A0_7}));
  // _8_bit_Latch__LVC573 8_bit_latch_lvc573_1: pin names not known; wires that end beside it: pull_resistor_14_node, microprocessor_w65c816_1_p8, BANK_LATCH, BA0_7
  // _8_bit_Bus_Transceiver__LVC4245 8_bit_bus_transceiver_lvc4245_1: pin names not known; wires that end beside it: DATA_TRANSMIT_B, microprocessor_w65c816_1_p8, RWB, D
  // _8_bit_Latch__LVC573 8_bit_latch_lvc573_2: pin names not known; wires that end beside it: pull_resistor_13_node, pull_resistor_6_node, nor_1_out, USER_BANK
  D_Flip_Flop #(.trigger("high")) d_ff_1 (
    .clk(or_4_out), .D(or_5_out), .Q(KERNAL_MODE), .Qn(KERNAL_MODE_B));  // open: preset, reset
  // _8_bit_Latch__LVC573 8_bit_latch_lvc573_3: pin names not known; wires that end beside it: pull_resistor_15_node, D, nor_2_out, OUT_INTERRUPTS
  not not_31 (RWB_B, RWB);
  and and_9 (FETCH_OPCODE, microprocessor_w65c816_1_p11, microprocessor_w65c816_1_p12);
  or or_6 (VALID_ADDRESS, microprocessor_w65c816_1_p11, microprocessor_w65c816_1_p12);
  // Probe on BA0_7
  // Probe on D
  // _16_bit_Line_Driver__LVC16244 16_bit_line_driver_lvc16244_1: pin names not known; wires that end beside it: or_1_out, or_1_out, or_2_out, or_2_out, USER_BANK[7:4], USER_BANK[3:0], 4'b0000, {3'b000, KERNAL_MODE}, D[7:4], D[3:0], D[7:4], D[3:0]
  // _8_bit_Line_Driver__LVC541 8_bit_line_driver_lvc541_1: pin names not known; wires that end beside it: or_3_out, or_3_out, OUT_INTERRUPTS, D
  // Probe on USER_BANK
  // Probe on KERNAL_MODE
  // Probe on OUT_INTERRUPTS
  // Probe on {BA0_7[0], A8_15, IRAM_A0_7}
  Internal_Memory_Glue internal_memory_glue_1 (
    .WEB(internal_memory_glue_1_web), .CEB(internal_memory_glue_1_ceb),
    .ADDRESS_OUT_A0_16(internal_memory_glue_1_address_out_a0_16), .OEB(internal_memory_glue_1_oeb),
    .USER_BANK(USER_BANK), .BA0_7(BA0_7), .ADDRESS_IN_A0_16({BA0_7[0], A8_15, IRAM_A0_7}),
    .KERNAL_MODE_B(KERNAL_MODE_B), .KERNAL_MODE(KERNAL_MODE),
    .DEVICE_ADDRESS_VALID_B(DEVICE_ADDRESS_VALID_B), .ADDRESS_IN_FIRST_128K(A_128K),
    .READ_ENABLE(READ_ENABLE), .READ_BANK_REMAP(READ_BANK_REMAP), .WRITE_ENABLE(WRITE_ENABLE));
  // Probe on internal_memory_glue_1_address_out_a0_16
  RAM #(.addrWidth(17), .databus("bidir"), .enables("line"), .trigger("high"), .\type ("nonvolatile")) ram_1 (
    .addr(internal_memory_glue_1_address_out_a0_16), .data(D));  // open: we, oe, clk
  // NOT_Gate not_32 has open pins: in=internal_memory_glue_1_oeb, out=open
  // NOT_Gate not_33 has open pins: in=internal_memory_glue_1_web, out=open
  // NOT_Gate not_34 has open pins: in=internal_memory_glue_1_ceb, out=open
  // _8_bit_Latch__LVC573 8_bit_latch_lvc573_4: pin names not known; wires that end beside it: KERNAL_MODE, D, READ_BANK_REMAP, MRAM_A16_23
  // _8_bit_Line_Driver__LVC541 8_bit_line_driver_lvc541_2: pin names not known; wires that end beside it: KERNAL_MODE_B, KERNAL_MODE_B, BA0_7, MRAM_A16_23
  and and_10 (and_10_out, A_128K_B, KERNAL_MODE, VALID_ADDRESS);
  and and_11 (and_11_out, VALID_ADDRESS, KERNAL_MODE_B);
  // Probe on MRAM_A16_23
  nor nor_4 (MRAM_VALID_ADDRESS_B, and_10_out, and_11_out);
  or or_7 (MRAM_VALID_ADDRESS, and_10_out, and_11_out);
  // Probe on D
  assign buffer_2_out = D;  // Buffer buffer_2, 8 bits wide
  or or_8 (or_8_out, READ_ENABLE_B, MRAM_VALID_ADDRESS_B);
  or or_9 (or_9_out, WRITE_ENABLE_B, MRAM_VALID_ADDRESS_B);
  Pull_Resistor pull_resistor_17 (.node(buffer_2_out));
  Pull_Resistor pull_resistor_18 (.node(pull_resistor_18_node));
  Pull_Resistor #(.pull(1)) pull_resistor_19 (.node(pull_resistor_19_node));
  Pull_Resistor pull_resistor_20 (.node(pull_resistor_20_node));
  Pull_Resistor #(.pull(1)) pull_resistor_21 (.node(pull_resistor_21_node));
  // _3_to_8_Decoder__LVC138 3_to_8_decoder_lvc138_3: pin names not known; wires that end beside it: pull_resistor_20_node, pull_resistor_20_node, MRAM_A[23:21], pull_resistor_21_node, {n3_to_8_decoder_lvc138_3_p5, CS3_B, CS2_B, CS1_B, CS0_B}
  // _8_bit_Bi_latch__LVC543 8_bit_bi_latch_lvc543_1: pin names not known; wires that end beside it: RWB_B, or_9_out, pull_resistor_18_node, buffer_2_out, n8_bit_bi_latch_lvc543_1_p5, RWB, or_8_out, n8_bit_bi_latch_lvc543_1_p8
  // _16_bit_Line_Driver__LVC16244 16_bit_line_driver_lvc16244_2: pin names not known; wires that end beside it: pull_resistor_19_node, MRAM_ACCESS_B, MRAM_ACCESS_B, MRAM_ACCESS_B, {RDY, MRAM_VALID_ADDRESS, RWB_B, RWB}, MRAM_A16_23[3:0], MRAM_A16_23[7:4], {MREADY, MVALID, MWRITE, MREAD}, MRAM_A[19:16], MRAM_A[23:20]
  // _16_bit_Line_Driver__LVC16244 16_bit_line_driver_lvc16244_3: pin names not known; wires that end beside it: MRAM_ACCESS_B, MRAM_ACCESS_B, MRAM_ACCESS_B, MRAM_ACCESS_B, A8_15[7:4], A8_15[3:0], A0_7[7:4], A0_7[3:0], MRAM_A[15:12], MRAM_A[11:8], MRAM_A[7:4], MRAM_A[3:0]
  Pull_Resistor pull_resistor_22 (.node(n8_bit_bi_latch_lvc543_1_p8));
  Pull_Resistor pull_resistor_23 (.node(MREAD));
  Pull_Resistor pull_resistor_24 (.node(MWRITE));
  Pull_Resistor pull_resistor_25 (.node(MVALID));
  Pull_Resistor pull_resistor_26 (.node(MREADY));
  // Probe on MRAM_A
  nand nand_7 (nand_7_out, MREAD, MVALID);
  nand nand_8 (nand_8_out, MWRITE, MVALID);
  // Probe on MRAM_A[20:0]
  RAM #(.addrWidth(21), .databus("bidir"), .enables("line"), .trigger("high"), .\type ("nonvolatile")) ram_2 (
    .addr(MRAM_A[20:0]), .data(n8_bit_bi_latch_lvc543_1_p5));  // open: we, oe, clk
  // NOT_Gate not_35 has open pins: in=nand_7_out, out=open
  // NOT_Gate not_36 has open pins: in=nand_8_out, out=open
  // NOT_Gate not_37 has open pins: in=CS0_B, out=open
  RAM #(.addrWidth(21), .databus("bidir"), .enables("line"), .trigger("high"), .\type ("nonvolatile")) ram_3 (
    .addr(MRAM_A[20:0]), .data(ram_3_data));  // open: we, oe, clk
  // NOT_Gate not_38 has open pins: in=nand_7_out, out=open
  // NOT_Gate not_39 has open pins: in=nand_8_out, out=open
  // NOT_Gate not_40 has open pins: in=CS1_B, out=open
  RAM #(.addrWidth(21), .databus("bidir"), .enables("line"), .trigger("high"), .\type ("nonvolatile")) ram_4 (
    .addr(MRAM_A[20:0]), .data(ram_3_data));  // open: we, oe, clk
  // NOT_Gate not_41 has open pins: in=nand_7_out, out=open
  // NOT_Gate not_42 has open pins: in=nand_8_out, out=open
  // NOT_Gate not_43 has open pins: in=CS2_B, out=open
  RAM #(.addrWidth(21), .databus("bidir"), .enables("line"), .trigger("high"), .\type ("nonvolatile")) ram_5 (
    .addr(MRAM_A[20:0]), .data(ram_3_data));  // open: we, oe, clk
  // NOT_Gate not_44 has open pins: in=nand_7_out, out=open
  // NOT_Gate not_45 has open pins: in=nand_8_out, out=open
  // NOT_Gate not_46 has open pins: in=CS3_B, out=open

  // Other names for the same wires on the sheet: SEL8 = MRAM_ACCESS_B; IRAM_A16 = BA0_7[0]; MRAM_A0_7[7:0] = A0_7;
  //   IRAM_A8_15[7:0] = A8_15; MRAM_A8_15[7:0] = A8_15; MRAM_A0_20[20:0] = MRAM_A[20:0]

  // Notes on the sheet:
  //   Device Decode (F000 to F7FF)
  //   Bank Decode
  //   The lines with the pull resistors should be connected but the simulator is wonky during writes if they are.
  //   bits 0..3 all zero
  //   bits 4..7 all zero
  //   bits 1..3 all zero
  //   Internal Device Select
  //   IDevice0 Address Select
  //   Kernal Mode (Internal Device 0 Address 0)
  //   User Bank (Internal Device 0 Address 1)
  //   Interrupts being output (Internal Device 0 Address 3)
endmodule

module Timing_Circuit (
  input  RESET,
  output [9:0] SELECTOR,
  output RST,
  output RST_1,
  output CLK,
  output CLK_B,
  output HCLK,
  output HCLK_B,
  output [4:0] MULTIPLEXER,
  output [3:0] COUNTER,
  output RSTB
);

  wire and_1_out, clock_1_out, clock_2_out, clock_3_out, d_ff_4_q, d_ff_5_q, nand_1_out, not_1_out,
       not_2_out, not_3_out, not_4_out, not_5_out, pull_resistor_1_node, pull_resistor_2_node,
       pull_resistor_3_node, pull_resistor_4_node, pull_resistor_5_node, pull_resistor_6_node;
  wire [7:5] n3_to_8_decoder_lvc138_1_p5, n8_bit_latch_lvc574_1_p4, n8_bit_latch_lvc574_2_p4;

  Clock clock_1 (.out(clock_1_out));
  not not_1 (not_1_out, RESET);
  Clock clock_2 (.out(clock_2_out));
  Clock clock_3 (.out(clock_3_out));
  // Digital_Oscilloscope #(.nState(32)) digital_oscilloscope_1: pin names not known; wires that end beside it: clock_3_out, SELECTOR[0], SELECTOR[1], SELECTOR[2], SELECTOR[3], SELECTOR[4], SELECTOR[5], SELECTOR[6], SELECTOR[7], SELECTOR[8], SELECTOR[9]
  // EconoReset__DS1813 econoreset_ds1813_1: pin names not known; wires that end beside it: not_1_out, clock_2_out, RSTB
  not not_2 (not_2_out, RSTB);
  D_Flip_Flop d_ff_1 (.clk(clock_1_out), .D(CLK_B), .Q(CLK), .Qn(CLK_B), .reset(not_2_out));  // open: preset
  D_Flip_Flop d_ff_2 (.clk(CLK_B), .D(HCLK_B), .Q(HCLK), .Qn(HCLK_B), .reset(not_2_out));  // open: preset
  D_Flip_Flop d_ff_3 (.clk(CLK), .D(RSTB), .Q(RST), .reset(not_2_out));  // open: Qn, preset
  D_Flip_Flop d_ff_4 (.clk(CLK), .D(RST), .Q(d_ff_4_q), .reset(not_2_out));  // open: Qn, preset
  D_Flip_Flop d_ff_5 (.clk(CLK), .D(d_ff_4_q), .Q(d_ff_5_q), .reset(not_2_out));  // open: Qn, preset
  D_Flip_Flop d_ff_6 (.clk(CLK), .D(d_ff_5_q), .Q(RST_1), .reset(not_2_out));  // open: Qn, preset
  and and_1 (and_1_out, nand_1_out, RST_1);
  Pull_Resistor #(.pull(1)) pull_resistor_1 (.node(pull_resistor_1_node));
  Pull_Resistor #(.pull(1)) pull_resistor_2 (.node(pull_resistor_2_node));
  Pull_Resistor #(.pull(1)) pull_resistor_3 (.node(pull_resistor_3_node));
  // _4_bit_Counter__LVC163 4_bit_counter_lvc163_1: pin names not known; wires that end beside it: and_1_out, pull_resistor_1_node, pull_resistor_2_node, CLK, pull_resistor_3_node, RST_1, COUNTER
  nand nand_1 (nand_1_out, not_3_out, not_4_out, COUNTER[2], not_5_out);
  not not_3 (not_3_out, COUNTER[0]);
  not not_4 (not_4_out, COUNTER[1]);
  not not_5 (not_5_out, COUNTER[3]);
  Pull_Resistor pull_resistor_4 (.node(pull_resistor_4_node));
  // _3_to_8_Decoder__LVC138 3_to_8_decoder_lvc138_1: pin names not known; wires that end beside it: COUNTER[3], pull_resistor_4_node, COUNTER[2:0], RST_1, {n3_to_8_decoder_lvc138_1_p5, MULTIPLEXER}
  Pull_Resistor pull_resistor_5 (.node(pull_resistor_5_node));
  Pull_Resistor pull_resistor_6 (.node(pull_resistor_6_node));
  // _8_bit_Latch__LVC574 8_bit_latch_lvc574_1: pin names not known; wires that end beside it: pull_resistor_5_node, {n3_to_8_decoder_lvc138_1_p5, MULTIPLEXER}, CLK_B, {n8_bit_latch_lvc574_1_p4, SELECTOR[8], SELECTOR[6], SELECTOR[4], SELECTOR[2], SELECTOR[0]}
  // _8_bit_Latch__LVC574 8_bit_latch_lvc574_2: pin names not known; wires that end beside it: pull_resistor_6_node, {n8_bit_latch_lvc574_1_p4, SELECTOR[8], SELECTOR[6], SELECTOR[4], SELECTOR[2], SELECTOR[0]}, CLK, {n8_bit_latch_lvc574_2_p4, SELECTOR[9], SELECTOR[7], SELECTOR[5], SELECTOR[3], SELECTOR[1]}
  Pull_Resistor #(.pull(1)) pull_resistor_7 (.node(n8_bit_latch_lvc574_1_p4[7]));
  Pull_Resistor #(.pull(1)) pull_resistor_8 (.node(n8_bit_latch_lvc574_1_p4[6]));
  Pull_Resistor #(.pull(1)) pull_resistor_9 (.node(n8_bit_latch_lvc574_1_p4[5]));
  Pull_Resistor #(.pull(1)) pull_resistor_10 (.node(n8_bit_latch_lvc574_2_p4[7]));
  Pull_Resistor #(.pull(1)) pull_resistor_11 (.node(n8_bit_latch_lvc574_2_p4[6]));
  Pull_Resistor #(.pull(1)) pull_resistor_12 (.node(n8_bit_latch_lvc574_2_p4[5]));

  // Other names for the same wires on the sheet: CLOCK_B = CLK_B; HALF_CLOCK = HCLK; HALF_CLOCK_B = HCLK_B;
  //   RESET_0 = RST; RESET_1 = RST_1; SEL0 = SELECTOR[0]; SEL1 = SELECTOR[1]; SEL2 = SELECTOR[2]; SEL3 = SELECTOR[3];
  //   SEL4 = SELECTOR[4]; SEL5 = SELECTOR[5]; SEL6 = SELECTOR[6]; SEL7 = SELECTOR[7]; SEL8 = SELECTOR[8];
  //   SEL9 = SELECTOR[9]

  // Notes on the sheet:
  //   Debug Outputs
endmodule

module Interrupt_Vectoring (
  input  [7:0] ADDRESS_IN_A0_7,
  input  VPB,
  input  IRQ_0_B,
  input  IRQ_1_B,
  input  IRQ_2_B,
  input  IRQ_3_B,
  input  IRQ_4_B,
  input  IRQ_5_B,
  input  IRQ_6_B,
  input  IRQ_7_B,
  input  NMI_0_B,
  input  NMI_1_B,
  input  NMI_2_B,
  input  NMI_3_B,
  output [7:0] ADDRESS_OUT_A0_7,
  output IRQ_B,
  output NMI_B
);

  wire n8_to_3_encoder_ls148_1_p4, n8_to_3_encoder_ls148_2_p4, nand_1_out, nand_2_out, not_1_out, not_2_out,
       not_3_out, not_4_out, pull_resistor_5_node, pull_resistor_6_node;
  wire [0:0] n8_bit_latch_lvc573_1_p4, n8_bit_latch_lvc573_2_p4, n8_bit_line_driver_lvc541_1_p4;
  wire [2:0] n8_to_3_encoder_ls148_1_p3, n8_to_3_encoder_ls148_2_p3;
  wire [3:0] pull_resistor_4_node;

  not not_1 (not_1_out, VPB);
  Pull_Resistor #(.pull(1)) pull_resistor_1 (.node(pull_resistor_4_node[3]));
  Pull_Resistor #(.pull(1)) pull_resistor_2 (.node(pull_resistor_4_node[2]));
  Pull_Resistor #(.pull(1)) pull_resistor_3 (.node(pull_resistor_4_node[1]));
  Pull_Resistor #(.pull(1)) pull_resistor_4 (.node(pull_resistor_4_node[0]));
  not not_2 (not_2_out, nand_1_out);
  nand nand_1 (nand_1_out, ADDRESS_IN_A0_7[1], ADDRESS_IN_A0_7[2], ADDRESS_IN_A0_7[3], not_1_out);
  not not_3 (not_3_out, ADDRESS_IN_A0_7[2]);
  nand nand_2 (nand_2_out, ADDRESS_IN_A0_7[1], not_3_out, ADDRESS_IN_A0_7[3], not_1_out);
  Pull_Resistor pull_resistor_5 (.node(pull_resistor_5_node));
  not not_4 (not_4_out, nand_2_out);
  Pull_Resistor pull_resistor_6 (.node(pull_resistor_6_node));
  // _8_to_3_Encoder__LS148 8_to_3_encoder_ls148_1: pin names not known; wires that end beside it: pull_resistor_5_node, {IRQ_0_B, IRQ_1_B, IRQ_2_B, IRQ_3_B, IRQ_4_B, IRQ_5_B, IRQ_6_B, IRQ_7_B}, n8_to_3_encoder_ls148_1_p3, n8_to_3_encoder_ls148_1_p4, IRQ_B
  // _8_to_3_Encoder__LS148 8_to_3_encoder_ls148_2: pin names not known; wires that end beside it: pull_resistor_6_node, {NMI_0_B, NMI_1_B, NMI_2_B, NMI_3_B, pull_resistor_4_node}, n8_to_3_encoder_ls148_2_p3, n8_to_3_encoder_ls148_2_p4, NMI_B
  // Probe on {4'b1101, n8_to_3_encoder_ls148_1_p3, 1'b0}
  // Probe on {4'b1100, n8_to_3_encoder_ls148_2_p3, 1'b0}
  // _8_bit_Line_Driver__LVC541 8_bit_line_driver_lvc541_1: pin names not known; wires that end beside it: not_2_out, not_4_out, ADDRESS_IN_A0_7, {ADDRESS_OUT_A0_7[7:1], n8_bit_line_driver_lvc541_1_p4[0]}
  // _8_bit_Latch__LVC573 8_bit_latch_lvc573_1: pin names not known; wires that end beside it: nand_1_out, {4'b1101, n8_to_3_encoder_ls148_1_p3, 1'b0}, n8_to_3_encoder_ls148_1_p4, {ADDRESS_OUT_A0_7[7:1], n8_bit_latch_lvc573_1_p4[0]}
  // _8_bit_Latch__LVC573 8_bit_latch_lvc573_2: pin names not known; wires that end beside it: nand_2_out, {4'b1100, n8_to_3_encoder_ls148_2_p3, 1'b0}, n8_to_3_encoder_ls148_2_p4, {ADDRESS_OUT_A0_7[7:1], n8_bit_latch_lvc573_2_p4[0]}

  assign ADDRESS_OUT_A0_7[0] = ADDRESS_IN_A0_7[0];
endmodule

module Internal_Memory_Glue (
  input  [7:0] USER_BANK,
  input  [7:0] BA0_7,
  input  [16:0] ADDRESS_IN_A0_16,
  input  KERNAL_MODE_B,
  input  KERNAL_MODE,
  input  DEVICE_ADDRESS_VALID_B,
  input  ADDRESS_IN_FIRST_128K,
  input  READ_ENABLE,
  input  READ_BANK_REMAP,
  input  WRITE_ENABLE,
  output [16:0] ADDRESS_OUT_A0_16,
  output OEB,
  output WEB,
  output CEB
);

  wire nand_1_out, pull_resistor_1_node;

  Pull_Resistor #(.pull(1)) pull_resistor_1 (.node(pull_resistor_1_node));
  // _4_bit_Line_Driver__LVC125 4_bit_line_driver_lvc125_1: pin names not known; wires that end beside it: KERNAL_MODE, KERNAL_MODE_B, pull_resistor_1_node, pull_resistor_1_node, 1'b1, ADDRESS_IN_A0_16[16], ADDRESS_OUT_A0_16[16], ADDRESS_OUT_A0_16[16]
  // _16_bit_Line_Driver__LVC16244 16_bit_line_driver_lvc16244_1: pin names not known; wires that end beside it: KERNAL_MODE, KERNAL_MODE, KERNAL_MODE, KERNAL_MODE, USER_BANK[7:4], USER_BANK[3:0], BA0_7[7:4], BA0_7[3:0], ADDRESS_OUT_A0_16[15:12], ADDRESS_OUT_A0_16[11:8], ADDRESS_OUT_A0_16[7:4], ADDRESS_OUT_A0_16[3:0]
  // _16_bit_Line_Driver__LVC16244 16_bit_line_driver_lvc16244_2: pin names not known; wires that end beside it: KERNAL_MODE_B, KERNAL_MODE_B, KERNAL_MODE_B, KERNAL_MODE_B, ADDRESS_IN_A0_16[15:12], ADDRESS_IN_A0_16[11:8], ADDRESS_IN_A0_16[7:4], ADDRESS_IN_A0_16[3:0], ADDRESS_OUT_A0_16[15:12], ADDRESS_OUT_A0_16[11:8], ADDRESS_OUT_A0_16[7:4], ADDRESS_OUT_A0_16[3:0]
  nand nand_1 (nand_1_out, DEVICE_ADDRESS_VALID_B, ADDRESS_IN_FIRST_128K, READ_ENABLE, KERNAL_MODE);
  nand nand_2 (WEB, KERNAL_MODE, ADDRESS_IN_FIRST_128K, DEVICE_ADDRESS_VALID_B, WRITE_ENABLE);
  or or_1 (OEB, nand_1_out, READ_BANK_REMAP);
  Pull_Resistor pull_resistor_2 (.node(CEB));
endmodule
